# Fritzing sketch MysteryMachine2 (saved by Fritzing 0.8.5b)
circuit board: 16cm x 10cm
breadboards: 1

parts:
  Onderdeel1 = Arduino Uno (Rev3)
  R_LC = Resistor [tolerance=±5% resistance=1k package=THT]
  T1 = Toggle Switch [package=THT]
  T2 = Toggle Switch [package=THT]
  RotSwitch1 = female pin header, 6 pins [form="♀ (female)"]
  R1_1 = Resistor [tolerance=±5% resistance=10k package=THT]
  R1_3 = Resistor [tolerance=±5% resistance=10k package=THT]
  R1_4 = Resistor [tolerance=±5% resistance=10k package=THT]
  R1_5 = Resistor [tolerance=±5% resistance=10k package=THT]
  R_L1 = Resistor [tolerance=±5% resistance=1k package=THT]
  R1_2 = Resistor [tolerance=±5% resistance=10k package=THT]
  RotSwitch2 = female pin header, 6 pins [form="♀ (female)"]
  R2_1 = Resistor [tolerance=±5% resistance=10k package=THT]
  R_L2 = Resistor [tolerance=±5% resistance=1k package=THT]
  R2_4 = Resistor [tolerance=±5% resistance=10k package=THT]
  R2_5 = Resistor [tolerance=±5% resistance=10k package=THT]
  R2_2 = Resistor [tolerance=±5% resistance=10k package=THT]
  R2_3 = Resistor [tolerance=±5% resistance=10k package=THT]
  S1 = Pushbutton [package="[THT]"]
  S2 = Pushbutton [package="[THT]"]
  L2_6 = LED - 5mm [color="Red (633nm)" package="5 mm [THT]"]
  L1_6 = LED - 5mm [color="Red (633nm)" package="5 mm [THT]"]
  L2_7 = LED - 5mm [color="Orange (612nm)" package="5 mm [THT]"]
  L1_7 = LED - 5mm [color="Orange (612nm)" package="5 mm [THT]"]
  L2_8 = LED - 5mm [color="Green (565nm)" package="5 mm [THT]"]
  L1_8 = LED - 5mm [color="Green (565nm)" package="5 mm [THT]"]
  L2_9 = LED - 5mm [color="Yellow (585nm)" package="5 mm [THT]"]
  L1_9 = LED - 5mm [color="Yellow (585nm)" package="5 mm [THT]"]
  L2_10 = LED - 5mm [color="Blue (505nm)" package="5 mm [THT]"]
  L1_10 = LED - 5mm [color="Blue (505nm)" package="5 mm [THT]"]
  L_3 = LED - 5mm [color="Red (633nm)" package="5 mm [THT]"]
  L_Mid1 = LED - 5mm [color="Red (633nm)" package="5 mm [THT]"]
  L_4 = LED - 5mm [color="Red (633nm)" package="5 mm [THT]"]

nets:
  N1: Onderdeel1.A0, RotSwitch1.pin1, R1_1.Pin_0, L1_6.anode
  N2: Onderdeel1.A1, RotSwitch1.pin2, R1_2.Pin_0, L1_7.anode
  N3: Onderdeel1.A2, RotSwitch1.pin3, R1_3.Pin_0, L1_9.anode
  N4: Onderdeel1.A3, RotSwitch1.pin4, R1_4.Pin_0, L1_8.anode
  N5: Onderdeel1.A4/SDA, RotSwitch1.pin5, R1_5.Pin_0, L1_10.anode
  N6: Onderdeel1.A5/SCL, Onderdeel1.GND, R_LC.Pin_1, T2.COM, RotSwitch1.pin6, R1_1.Pin_1, R1_3.Pin_1, R1_4.Pin_1, R1_5.Pin_1, R_L1.Pin_1, R1_2.Pin_1, RotSwitch2.pin6, R2_1.Pin_1, R_L2.Pin_1, R2_4.Pin_1, R2_5.Pin_1, R2_2.Pin_1, R2_3.Pin_1, S1.Pin_3, S1.Pin_4, S2.Pin_1, S2.Pin_2
  N7: Onderdeel1.D8, RotSwitch2.pin1, R2_1.Pin_0, L2_6.anode
  N8: Onderdeel1.D9_PWM, RotSwitch2.pin2, R2_2.Pin_0, L2_7.anode
  N9: Onderdeel1.D10_PWM/SS, RotSwitch2.pin3, R2_3.Pin_0, L2_9.anode
  N10: Onderdeel1.D11_PWM/MOSI, RotSwitch2.pin4, R2_4.Pin_0, L2_8.anode
  N11: Onderdeel1.D12/MISO, RotSwitch2.pin5, R2_5.Pin_0, L2_10.anode
  N12: Onderdeel1.D2, L_4.anode
  N13: Onderdeel1.D3_PWM, L_Mid1.anode
  N14: Onderdeel1.D4, L_3.anode
  N15: Onderdeel1.5V, T1.COM
  N16: R_LC.Pin_0, L_3.cathode, L_Mid1.cathode, L_4.cathode
  N17: T1.L1, T2.L1
  N18: T1.L2, T2.L2
  N19: R_L1.Pin_0, L1_6.cathode, L1_7.cathode, L1_8.cathode, L1_9.cathode, L1_10.cathode
  N20: R_L2.Pin_0, L2_6.cathode, L2_7.cathode, L2_8.cathode, L2_9.cathode, L2_10.cathode
  N21: S1.Pin_1, S1.Pin_2, S2.Pin_3, S2.Pin_4

notes:
  The monopolar rotary switch is connected as such:
  1: Red, RS_1, A0/8
  2: Orange, RS_2, A1/9
  3: Yellow, RS_3, A2/10
  4: Green, RS_4, A3/11
  5: Cyan, RS_5, A4/12
  6: +5V, RS_A (the pole)
  Goals are
  (1) supply an LED with power, bypassing the Arduino
  (2) let the Arduino detect which choice is made
  Of these three LEDs, one will be turned on, when both pushbuttons are pressed
